// Logisim project project3.circ as structural Verilog: 2 circuits, main circuit main
// T0
module main (
  input  in_1
);

  wire IR_E, IR_LH, MEM_CLR, MEM_LD, MEM_SEL, MEM_STR, T0, T1, T2, T3, T4, T5, T6, T7;
  wire [1:0] AR_FS, AR_OCS, AR_ODS, IR_FS, MuxBSel;
  wire [3:0] AR_RS;

  counter counter_1 (
    .out_2(T0), .out_3(T1), .out_4(T2), .out_5(T3), .out_6(T4), .out_7(T5), .out_8(T6), .out_9(T7),
    .in_1(in_1));
  assign IR_LH = T0 ? 1'b0 : 1'bz;  // Controlled_Buffer controlled_buffer_1
  assign IR_E = T0 ? 1'b1 : 1'bz;  // Controlled_Buffer controlled_buffer_2
  assign IR_FS = T0 ? 2'b11 : 2'bz;  // Controlled_Buffer controlled_buffer_3
  assign AR_FS = T0 ? 2'b01 : 2'bz;  // Controlled_Buffer controlled_buffer_4
  assign AR_RS = T0 ? 4'b0010 : 4'bz;  // Controlled_Buffer controlled_buffer_5
  assign AR_OCS = T0 ? 2'b00 : 2'bz;  // Controlled_Buffer controlled_buffer_6
  assign AR_ODS = T0 ? 2'b00 : 2'bz;  // Controlled_Buffer controlled_buffer_7
  assign MEM_STR = T0 ? 1'b0 : 1'bz;  // Controlled_Buffer controlled_buffer_8
  assign MEM_SEL = T0 ? 1'b1 : 1'bz;  // Controlled_Buffer controlled_buffer_9
  assign MEM_LD = T0 ? 1'b1 : 1'bz;  // Controlled_Buffer controlled_buffer_10
  assign MEM_CLR = T0 ? 1'b0 : 1'bz;  // Controlled_Buffer controlled_buffer_11
  assign MuxBSel = T0 ? 2'b10 : 2'bz;  // Controlled_Buffer controlled_buffer_12
  assign IR_LH = T1 ? 1'b0 : 1'bz;  // Controlled_Buffer controlled_buffer_13
  assign IR_E = T1 ? 1'b1 : 1'bz;  // Controlled_Buffer controlled_buffer_14
  assign IR_FS = T1 ? 2'b11 : 2'bz;  // Controlled_Buffer controlled_buffer_15
  assign AR_FS = T1 ? 2'b01 : 2'bz;  // Controlled_Buffer controlled_buffer_16
  assign AR_RS = T1 ? 4'b0001 : 4'bz;  // Controlled_Buffer controlled_buffer_17
  assign AR_OCS = T1 ? 2'b00 : 2'bz;  // Controlled_Buffer controlled_buffer_18
  assign AR_ODS = T1 ? 2'b01 : 2'bz;  // Controlled_Buffer controlled_buffer_19
  assign MEM_STR = T1 ? 1'b0 : 1'bz;  // Controlled_Buffer controlled_buffer_20
  assign MEM_SEL = T1 ? 1'b1 : 1'bz;  // Controlled_Buffer controlled_buffer_21
  assign MEM_LD = T1 ? 1'b1 : 1'bz;  // Controlled_Buffer controlled_buffer_22
  assign MEM_CLR = T1 ? 1'b0 : 1'bz;  // Controlled_Buffer controlled_buffer_23
  assign MuxBSel = T1 ? 2'b10 : 2'bz;  // Controlled_Buffer controlled_buffer_24
  assign IR_LH = T2 ? 1'b1 : 1'bz;  // Controlled_Buffer controlled_buffer_25
  assign IR_E = T2 ? 1'b1 : 1'bz;  // Controlled_Buffer controlled_buffer_26
  assign IR_FS = T2 ? 2'b11 : 2'bz;  // Controlled_Buffer controlled_buffer_27
  assign AR_FS = T2 ? 2'b01 : 2'bz;  // Controlled_Buffer controlled_buffer_28
  assign AR_RS = T2 ? 4'b0010 : 4'bz;  // Controlled_Buffer controlled_buffer_29
  assign AR_OCS = T2 ? 2'b00 : 2'bz;  // Controlled_Buffer controlled_buffer_30
  assign AR_ODS = T2 ? 2'b00 : 2'bz;  // Controlled_Buffer controlled_buffer_31
  assign MEM_STR = T2 ? 1'b0 : 1'bz;  // Controlled_Buffer controlled_buffer_32
  assign MEM_SEL = T2 ? 1'b1 : 1'bz;  // Controlled_Buffer controlled_buffer_33
  assign MEM_LD = T2 ? 1'b1 : 1'bz;  // Controlled_Buffer controlled_buffer_34
  assign MEM_CLR = T2 ? 1'b0 : 1'bz;  // Controlled_Buffer controlled_buffer_35
  assign MuxBSel = T2 ? 2'b10 : 2'bz;  // Controlled_Buffer controlled_buffer_36

  // Other names for the same wires on the sheet: SCR = in_1

  // Notes on the sheet:
  //   AR = M[PC]
  //   IR[0:7] = AR
  //   PC = PC + 1
  //   IR[0:7] = M[AR]
  //   AR = M[PC]
  //   IR[7:15] = AR
endmodule

module counter (
  input  in_1,
  output out_2,
  output out_3,
  output out_4,
  output out_5,
  output out_6,
  output out_7,
  output out_8,
  output out_9
);

  wire clock_1_out;
  wire [2:0] counter_1_q;

  Counter #(.width(3), .max('h7)) counter_1 (
    .Q(counter_1_q), .clk(clock_1_out), .clr(in_1));  // open: load, D, count, carry
  Clock clock_1 (.out(clock_1_out));
  Decoder #(.select(3), .enable("false")) decoder_1 (
    .out0(out_2), .out1(out_3), .out2(out_4), .out3(out_5), .out4(out_6), .out5(out_7), .out6(out_8),
    .out7(out_9), .sel(counter_1_q));
endmodule
